# Fritzing sketch Battary Test Device (saved by Fritzing 0.9.3b)
breadboards: 2

parts:
  Nokia_5110_LCD_Module1 = Nokia 5110 LCD
  Parça1 = Arduino Uno (Rev3)
  Up_=5 = Pushbutton [package="[THT]"]
  Down_=3 = Pushbutton [package="[THT]"]
  Select_=4 = Pushbutton [package="[THT]"]
  back_=7 = Pushbutton [package="[THT]"]
  R1 = Resistor [tolerance=±5% resistance=10k package=THT]
  R2 = Resistor [tolerance=±5% resistance=10k package=THT]
  R3 = Resistor [tolerance=±5% resistance=10k package=THT]
  R4 = Resistor [tolerance=±5% resistance=10k package=THT]
  R6 = Resistor [tolerance=±5% resistance=100k package=THT]
  R7 = Resistor [tolerance=±5% resistance=200k package=THT]
  J1 = Piezo Speaker

nets:
  N1: Nokia_5110_LCD_Module1.VCC, Parça1.D11_PWM/MOSI
  N2: Nokia_5110_LCD_Module1.GND, Parça1.D12/MISO
  N3: Nokia_5110_LCD_Module1.SCE, Parça1.D10_PWM/SS
  N4: Nokia_5110_LCD_Module1.RST, Parça1.D9_PWM
  N5: Nokia_5110_LCD_Module1.D/C, Parça1.D8
  N6: Nokia_5110_LCD_Module1.DN(MOSI), Parça1.3V3
  N7: Nokia_5110_LCD_Module1.SCLK, Parça1.D1/TX
  N8: Nokia_5110_LCD_Module1.LED, Nokia_5110_LCD_Module1.LED_(out), Parça1.GND, R1.Pin_1, R2.Pin_1, R3.Pin_1, R4.Pin_1, R6.Pin_0
  N9: Parça1.A0, R6.Pin_1, R7.Pin_0
  N10: Parça1.D2, J1.pin2
  N11: Parça1.D3_PWM, back_=7.Pin_1, back_=7.Pin_2, R4.Pin_0
  N12: Parça1.D4, Select_=4.Pin_1, Select_=4.Pin_2, R3.Pin_0
  N13: Parça1.D5_PWM, Down_=3.Pin_1, Down_=3.Pin_2, R1.Pin_0
  N14: Parça1.D6_PWM, Up_=5.Pin_1, Up_=5.Pin_2, R2.Pin_0
  N15: Parça1.5V, Up_=5.Pin_3, Up_=5.Pin_4, Down_=3.Pin_3, Down_=3.Pin_4, Select_=4.Pin_3, Select_=4.Pin_4, back_=7.Pin_3, back_=7.Pin_4

notes:
  yukaributon =6
  asagibuton =5
  secmebuton =4
  geributon =3
  R1 = 200.000k ohm
  R2 = 100.000k ohm

custom parts:
  Nokia 5110 LCD: Nokia 5110 Graphic 84*48 LCD module such as the Sparkfun LCD-10168 or the clones from Ebay. There is example code for the Arduino available from the Sparkfun site in https://learn.sparkfun.com/tutorials/graphic-lcd-hookup-guide This is a 3.3V device, if you are running it from a 5V micro you need a 5V tolorant level translator such as the 74ahc367 to protect the signal imputs. Rafa G. did a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
